# Fritzing sketch thermalLCD (saved by Fritzing 0.9.3b)
breadboards: 1

parts:
  Part1 = Arduino Uno (Rev3)
  R1 = Temperature Sensor (Thermistor) [thermistor_type=NTC package=THT]
  R2 = Resistor [tolerance=±5% resistance=10k package="0402 [SMD]"]
  LCM1602_IIC2 = LCM1602 IIC [part_number="LCM1602 IIC" chip_label="LCM1602 IIC" package="DIP (Dual Inline) [THT]"]
  U1 = LCD-16X2 [package=lcd-16x2]

nets:
  N1: Part1.A0, R1.pin_0, R2.Pin_0
  N2: Part1.A4/SDA, LCM1602_IIC2.SDA
  N3: Part1.A5/SCL, LCM1602_IIC2.SCL
  GND: Part1.GND, R2.Pin_1, LCM1602_IIC2.GND
  N4: R1.pin_1, LCM1602_IIC2.VCC
  VSS: LCM1602_IIC2.VSS, U1.VSS
  VDD: LCM1602_IIC2.VDD, U1.VDD
  N5: LCM1602_IIC2.V0, U1.VO
  N6: LCM1602_IIC2.RS, U1.RS
  N7: LCM1602_IIC2.RW, U1.R_W
  N8: LCM1602_IIC2.E, U1.E
  N9: LCM1602_IIC2.D0, U1.DB0
  N10: LCM1602_IIC2.D1, U1.DB1
  N11: LCM1602_IIC2.D2, U1.DB2
  N12: LCM1602_IIC2.D3, U1.DB3
  N13: LCM1602_IIC2.D4, U1.DB4
  N14: LCM1602_IIC2.D5, U1.DB5
  N15: LCM1602_IIC2.D6, U1.DB6
  N16: LCM1602_IIC2.D7, U1.DB7
  N17: LCM1602_IIC2.A, U1.A
  N18: LCM1602_IIC2.K, U1.K

custom parts:
  LCM1602 IIC: I2C-Module to use a 1602 or 2004 LCD on with the wire.h libory Serial LCD Modul

// code stored in the sketch: tempLCD.ino
/*
Termistor based temperature monitor with LCD display.
Requires:
- LCD display (ground, 5v, A4, A5)
- Termistor 
- Resistor (10k) 
Cicle: in -> termistor, out -> A0 , out -> 10k resistor, 10k resistor -> grnd)

*/

#include <Wire.h>
#include <LCD.h>
#include <LiquidCrystal_I2C.h>


int ThermistorPin = 0;
int Vo;
float R1 = 10000;
float logR2, R2, T;
float c1 = 1.009249522e-03, c2 = 2.378405444e-04, c3 = 2.019202697e-07;
                        
// The LCD constructor - address shown is 0x27 - may or may not be correct for yours
// Also based on YWRobot LCM1602 IIC V1
LiquidCrystal_I2C lcd(0x27, 2, 1, 0, 4, 5, 6, 7, 3, POSITIVE);  

void setup()
{
 
  lcd.begin(16,2); // sixteen characters across - 2 lines
  lcd.backlight();
  // first character - 1st line
  lcd.setCursor(0,0);
  lcd.print("Current temp:");
  
}
 
 
void loop()
{
  Vo = analogRead(ThermistorPin);
  // convert voltage to Kelvin and then subtract to get C
  R2 = R1 * (1023.0 / (float)Vo - 1.0);
  logR2 = log(R2);
  T = (1.0 / (c1 + c2*logR2 + c3*logR2*logR2*logR2));
  T = T - 273.15;

  // on 2nd line print temperature in far right
  // 8th character - 2nd line 
  lcd.setCursor(8,1);
  lcd.print(T); lcd.print("C");
  delay(500);                                      

}
